// Logisim project Laboratorio01_TCP.circ as structural Verilog: 9 circuits, main circuit main
module main (
);

  wire CLK1_out, CLK2, CLK3, paral2serial_1_clk, RESET;
  wire [6:0] paral2serial_1_serialoutput;
  wire [13:0] decaps_1_payload0, decaps_1_payload1, decaps_1_payload2, decaps_1_payload3;
  wire [15:0] message_dispatcher_1_serialoutput, packet_sorter_1_packet0, packet_sorter_1_packet1,
       packet_sorter_1_packet2, packet_sorter_1_packet3, PCKTA, PCKTB, PCKTC, PCKTD, serial2parals_1_packeta,
       serial2parals_1_packetb, serial2parals_1_packetc, serial2parals_1_packetd;

  Clock #(.highDuration(2), .lowDuration(2)) CLK1 (.out(CLK1_out));
  Button u_RESET (.out(RESET));
  not not_1 (CLK2, CLK1_out);
  Packet_Sorter packet_sorter_1 (
    .PacketA(PCKTA), .PacketB(PCKTB), .PacketC(PCKTC), .PacketD(PCKTD), .Packet0(packet_sorter_1_packet0),
    .Packet1(packet_sorter_1_packet1), .Packet2(packet_sorter_1_packet2), .Packet3(packet_sorter_1_packet3));
  Message_dispatcher message_dispatcher_1 (
    .CLK(CLK2), .Reset(RESET), .CLK_OUT(CLK3), .SerialOutput(message_dispatcher_1_serialoutput));
  Serial2Parals serial2parals_1 (
    .SerialInput(message_dispatcher_1_serialoutput), .CLK(CLK2), .Reset(RESET),
    .PacketA(serial2parals_1_packeta), .PacketB(serial2parals_1_packetb), .PacketC(serial2parals_1_packetc),
    .PacketD(serial2parals_1_packetd));
  Decaps decaps_1 (
    .Packet0(packet_sorter_1_packet0), .Packet1(packet_sorter_1_packet1), .Packet2(packet_sorter_1_packet2),
    .Packet3(packet_sorter_1_packet3), .Payload0(decaps_1_payload0), .Payload1(decaps_1_payload1),
    .Payload2(decaps_1_payload2), .Payload3(decaps_1_payload3));
  Register #(.width(16)) register_1 (.D(serial2parals_1_packeta), .Q(PCKTA), .clk(CLK3), .clr(RESET));  // open: en
  Register #(.width(16)) register_2 (.D(serial2parals_1_packetb), .Q(PCKTB), .clk(CLK3), .clr(RESET));  // open: en
  Register #(.width(16)) register_3 (.D(serial2parals_1_packetc), .Q(PCKTC), .clk(CLK3), .clr(RESET));  // open: en
  Register #(.width(16)) register_4 (.D(serial2parals_1_packetd), .Q(PCKTD), .clk(CLK3), .clr(RESET));  // open: en
  Paral2Serial paral2serial_1 (
    .Payload0(decaps_1_payload0), .Payload1(decaps_1_payload1), .Payload2(decaps_1_payload2),
    .Payload3(decaps_1_payload3), .Reset(RESET), .SerialOutput(paral2serial_1_serialoutput),
    .CLK(paral2serial_1_clk));
  TTY tty_1 (.data(paral2serial_1_serialoutput), .clk(paral2serial_1_clk), .clr(RESET));  // open: we
endmodule

module Packet_Sorter (
  input  [15:0] PacketA,
  input  [15:0] PacketB,
  input  [15:0] PacketC,
  input  [15:0] PacketD,
  output [15:0] Packet0,
  output [15:0] Packet1,
  output [15:0] Packet2,
  output [15:0] Packet3
);

  wire [15:0] packetorder2inputs_1_packetmax, packetorder2inputs_1_packetmin, packetorder2inputs_2_packetmax,
       packetorder2inputs_2_packetmin, packetorder2inputs_3_packetmax, packetorder2inputs_4_packetmin;

  PacketOrder2Inputs packetorder2inputs_1 (
    .PacketA(PacketA), .PacketB(PacketB), .PacketMin(packetorder2inputs_1_packetmin),
    .PacketMax(packetorder2inputs_1_packetmax));
  PacketOrder2Inputs packetorder2inputs_2 (
    .PacketA(PacketC), .PacketB(PacketD), .PacketMin(packetorder2inputs_2_packetmin),
    .PacketMax(packetorder2inputs_2_packetmax));
  PacketOrder2Inputs packetorder2inputs_3 (
    .PacketA(packetorder2inputs_1_packetmin), .PacketB(packetorder2inputs_2_packetmin), .PacketMin(Packet0),
    .PacketMax(packetorder2inputs_3_packetmax));
  PacketOrder2Inputs packetorder2inputs_4 (
    .PacketA(packetorder2inputs_1_packetmax), .PacketB(packetorder2inputs_2_packetmax),
    .PacketMin(packetorder2inputs_4_packetmin), .PacketMax(Packet3));
  PacketOrder2Inputs packetorder2inputs_5 (
    .PacketA(packetorder2inputs_3_packetmax), .PacketB(packetorder2inputs_4_packetmin), .PacketMin(Packet1),
    .PacketMax(Packet2));
endmodule

module PacketOrder2Inputs (
  input  [15:0] PacketA,
  input  [15:0] PacketB,
  output [15:0] PacketMin,
  output [15:0] PacketMax
);

  wire GT;

  Multiplexer #(.width(16)) multiplexer_1 (.in0(PacketA), .in1(PacketB), .out(PacketMin), .sel(GT));
  Multiplexer #(.width(16)) multiplexer_2 (.in0(PacketB), .in1(PacketA), .out(PacketMax), .sel(GT));
  BAOS baos_1 (.A(PacketA[15:14]), .B(PacketB[15:14]), .GT(GT));  // open: min, max

  // Other names for the same wires on the sheet: HeaderA[1:0] = PacketA[15:14]; HeaderB[1:0] = PacketB[15:14]
endmodule

module BAOS (
  input  [1:0] A,
  input  [1:0] B,
  output [1:0] min,
  output [1:0] max,
  output GT
);

  wire and_2_out, and_3_out, and_4_out, and_5_out, and_6_out, and_7_out, and_8_out, and_9_out, and_10_out,
       and_11_out, not_1_out, not_2_out, not_3_out;

  not not_1 (not_1_out, A[1]);
  not not_2 (not_2_out, B[1]);
  not not_3 (not_3_out, B[0]);
  and and_1 (min[1], A[1], B[1]);
  and and_2 (and_2_out, A[0], B[0]);
  and and_3 (and_3_out, not_1_out, A[0], B[1]);
  and and_4 (and_4_out, A[1], not_2_out, B[0]);
  or or_1 (max[1], B[1], A[1]);
  and and_5 (and_5_out, not_1_out, B[0]);
  and and_6 (and_6_out, A[0], not_2_out);
  and and_7 (and_7_out, B[1], B[0]);
  and and_8 (and_8_out, A[1], A[0]);
  and and_9 (and_9_out, A[0], not_2_out, not_3_out);
  and and_10 (and_10_out, A[1], not_2_out);
  and and_11 (and_11_out, A[1], A[0], not_3_out);
  or or_2 (min[0], and_2_out, and_3_out, and_4_out);
  or or_3 (max[0], and_5_out, and_6_out, and_7_out, and_8_out);
  or or_4 (GT, and_9_out, and_10_out, and_11_out);
endmodule

module Decaps (
  input  [15:0] Packet0,
  input  [15:0] Packet1,
  input  [15:0] Packet2,
  input  [15:0] Packet3,
  output [13:0] Payload0,
  output [13:0] Payload1,
  output [13:0] Payload2,
  output [13:0] Payload3
);


  assign Payload0 = Packet0[13:0];
  assign Payload1 = Packet1[13:0];
  assign Payload2 = Packet2[13:0];
  assign Payload3 = Packet3[13:0];
endmodule

module Serial2Parals (
  input  [15:0] SerialInput,
  input  CLK,
  input  Reset,
  output [15:0] PacketA,
  output [15:0] PacketB,
  output [15:0] PacketC,
  output [15:0] PacketD
);

  Register #(.width(16)) register_1 (.D(SerialInput), .clk(CLK), .Q(PacketD), .clr(Reset));  // open: en
  Register #(.width(16)) register_2 (.D(PacketD), .clk(CLK), .Q(PacketC), .clr(Reset));  // open: en
  Register #(.width(16)) register_3 (.D(PacketC), .clk(CLK), .Q(PacketB), .clr(Reset));  // open: en
  Register #(.width(16)) register_4 (.D(PacketB), .clk(CLK), .Q(PacketA), .clr(Reset));  // open: en
endmodule

module Paral2Serial (
  input  [13:0] Payload0,
  input  [13:0] Payload1,
  input  [13:0] Payload2,
  input  [13:0] Payload3,
  input  Reset,
  output [6:0] SerialOutput,
  output CLK
);

  wire [2:0] ff_counter_1_output_counter;

  FF_Counter ff_counter_1 (.Clear(Reset), .Output_Counter(ff_counter_1_output_counter), .CLK1(CLK));
  Multiplexer #(.select(3), .width(7)) multiplexer_1 (
    .in0(Payload0[13:7]), .in1(Payload0[6:0]), .in2(Payload1[13:7]), .in3(Payload1[6:0]),
    .in4(Payload2[13:7]), .in5(Payload2[6:0]), .in6(Payload3[13:7]), .in7(Payload3[6:0]), .out(SerialOutput),
    .sel(ff_counter_1_output_counter));

  // Other names for the same wires on the sheet: Char1[6:0] = Payload0[6:0]; Char0[6:0] = Payload0[13:7];
  //   Char3[6:0] = Payload1[6:0]; Char2[6:0] = Payload1[13:7]; Char5[6:0] = Payload2[6:0];
  //   Char4[6:0] = Payload2[13:7]; Char7[6:0] = Payload3[6:0]; Char6[6:0] = Payload3[13:7]
endmodule

module Message_dispatcher (
  input  CLK,
  input  Reset,
  output CLK_OUT,
  output [15:0] SerialOutput
);

  wire [1:0] Rndm;
  wire [5:0] CntrMsgs_q;
  wire [7:0] CntrPckts_q;
  wire [15:0] CharsPckt0, CharsPckt1, CharsPckt2, CharsPckt3;

  ROM #(.addrWidth(6), .dataWidth(64)) Messages (
    .addr(CntrMsgs_q), .data({CharsPckt0, CharsPckt1, CharsPckt2, CharsPckt3}));
  Counter #(.max('h3f), .width(6)) CntrMsgs (
    .count(1'b1), .Q(CntrMsgs_q), .up(1'b1), .clk(CLK_OUT), .clr(Reset));  // open: load, D, carry
  ROM #(.dataWidth(2)) RandomDispatch (.addr(CntrPckts_q), .data(Rndm));
  Counter CntrPckts (.count(1'b1), .Q(CntrPckts_q), .up(1'b1), .clk(CLK), .clr(Reset));  // open: load, D, carry
  and and_1 (CLK_OUT, ~CntrPckts_q[0], ~CntrPckts_q[1]);  // AND_Gate
  Multiplexer #(.select(2), .width(16)) multiplexer_1 (
    .in0({2'b00, CharsPckt0[14:8], CharsPckt0[6:0]}), .in1({2'b01, CharsPckt1[14:8], CharsPckt1[6:0]}),
    .in2({2'b10, CharsPckt2[14:8], CharsPckt2[6:0]}), .in3({2'b11, CharsPckt3[14:8], CharsPckt3[6:0]}),
    .out(SerialOutput), .sel(Rndm));

  // Other names for the same wires on the sheet: Pckt2[13:0] = {CharsPckt2[14:8], CharsPckt2[6:0]};
  //   Pckt0[13:0] = {CharsPckt0[14:8], CharsPckt0[6:0]}; Pckt1[13:0] = {CharsPckt1[14:8], CharsPckt1[6:0]};
  //   Pckt3[13:0] = {CharsPckt3[14:8], CharsPckt3[6:0]}; Slow_CLK = CLK_OUT

  // Notes on the sheet:
  //   contents of Messages (hex, n*v repeats v):
  //   63616d696e617461 6c6962657261646f 666f726d61646f72 736572656e617461 70616c6162726173
  //   656a656d706c6172 676f626965726e6f 6c61627261646f72 686162697475616c 636f6c756d6e6173
  //   6170657274757261 67656e65726f736f 6573636f6265726f 6772616261646f72 6d65726361646572
  //   6e6176656761646f 70726f677265736f 64656e6f73746172 666162756c6f736f 766572616e656172
  //   656d62616a616461 6f72717565737461 636f6c6563746172 65737472656e6172 70726f7465737461
  //   6361727265746561 696e746572696f72 6573636f6c746172 63656c6562726172 657374616c6c6172
  //   6661627269636172 666f7274756e6173 74656d65726f736f 616c7175696c6572 636f6272697a6f73
  //   696e737069726172 616365707461646f 656a65726369746f 6c69626572746164 6173706972696e61
  //   636f6e766572736f 726163696f6e616c 65766964656e7465 657363756c746f72 7265706f7361646f
  //   70726563696f7361 61636c616d61646f 6f62736572766172 706172616c656c61 7265636c616d6172
  //   636f6e6365646572 6170616369626c65 6469766572736173 746f7272656a6173 636f6d65646f7261
  //   726563657461646f 636f6e6563746172 6573636f6c746173 7472617461726f6e 636c617269646164
  //   636f6e6665736172 636f6e73756c6172 6465637265746f73 656c657661646f72
  //   contents of RandomDispatch (hex, n*v repeats v):
  //   1 3 0 2 0 2 1 3 0 1 2 3 1 0 3 2 3 2 0 1 1 3 0 2 3 0 2 1 1 0 3 2 0 3 1 2 0 2 3 1 3 2 1 0 0 1 2 3 0 3
  //   2 1 1 2 0 3 3 2 0 1 1 3 0 2 2 0 3 1 3 0 2 1 1 3 0 2 1 3 2 0 2 1 0 3 0 2 3 1 2 0 1 3 3 1 2 0 2 3 0 1
  //   2 0 3 1 1 2 0 3 1 0 2 3 0 2 3 1 3 0 2 1 0 1 2 3 3 0 2 1 0 1 2 3 3 2 0 1 2 0 1 3 2 1 3 0 0 3 1 2 2 3
  //   0 1 1 2 3 0 3 1 0 2 1 3 0 2 3 0 2 1 0 2 1 3 3 2 0 1 2 3 1 0 1 3 0 2 3 2 1 0 0 2 1 3 3 2 1 0 3 0 2 1
  //   1 0 2 3 3 1 2 0 1 2 0 3 3 0 1 2 3 0 1 2 2 3 1 0 3 2 1 0 1 2 0 3 0 2 1 3 2 1 3 0 3 1 2 0 0 1 3 2 1 2
  //   0 3 3 1 2
endmodule

module FF_Counter (
  input  Clear,
  output [2:0] Output_Counter,
  output CLK1
);

  wire FF0_qn, FF1_qn, FF2_qn, J1, J2, K2, Q1;

  and and_1 (J2, Q1, J1);
  and and_2 (K2, Q1, J1);
  Clock CLK0 (.out(CLK1));
  J_K_Flip_Flop FF2 (.J(J2), .K(K2), .clk(CLK1), .Qn(FF2_qn), .reset(Clear));  // open: Q, preset
  J_K_Flip_Flop FF1 (.J(J1), .K(J1), .clk(CLK1), .Q(Q1), .Qn(FF1_qn), .reset(Clear));  // open: preset
  J_K_Flip_Flop FF0 (.J(1'b1), .K(1'b1), .clk(CLK1), .Q(J1), .Qn(FF0_qn), .reset(Clear));  // open: preset
  not not_1 (Output_Counter[2], FF2_qn);
  not not_2 (Output_Counter[1], FF1_qn);
  not not_3 (Output_Counter[0], FF0_qn);

  // Other names for the same wires on the sheet: K1 = J1; Q0 = J1
endmodule
